// Logisim project simulation.circ as structural Verilog: 1 circuit, main circuit main
module main (
  input  in_1,
  input  in_2,
  output out_3,
  output out_4,
  output out_5,
  output out_6,
  output out_7,
  output out_8,
  output out_9,
  output out_10,
  output out_11
);

  wire and_1_out, and_2_out, and_3_out, and_4_out, and_5_out, and_6_out, and_7_out, and_8_out, and_9_out,
       and_10_out, and_11_out, and_12_out, and_13_out, and_14_out, and_15_out, and_16_out, and_17_out,
       buffer_1_out, buffer_2_out, buffer_3_out, clock_1_out, not_1_out, not_2_out, not_3_out, not_4_out,
       not_5_out, not_6_out, not_7_out, not_8_out, t_ff_2_q, t_ff_3_q, t_ff_4_q;

  Clock clock_1 (.out(clock_1_out));
  not not_1 (not_1_out, clock_1_out);
  not not_2 (not_2_out, out_3);
  not not_3 (not_3_out, t_ff_2_q);
  not not_4 (not_4_out, t_ff_3_q);
  T_Flip_Flop t_ff_1 (.clk(not_1_out), .T(not_1_out), .Q(out_3));  // open: Qn, preset, reset, en
  T_Flip_Flop t_ff_2 (.clk(not_2_out), .T(not_2_out), .Q(t_ff_2_q));  // open: Qn, preset, reset, en
  T_Flip_Flop t_ff_3 (.clk(not_3_out), .T(not_3_out), .Q(t_ff_3_q));  // open: Qn, preset, reset, en
  T_Flip_Flop t_ff_4 (.clk(not_4_out), .T(not_4_out), .Q(t_ff_4_q));  // open: Qn, preset, reset, en
  buf buffer_1 (buffer_1_out, t_ff_2_q);
  buf buffer_2 (buffer_2_out, t_ff_3_q);
  buf buffer_3 (buffer_3_out, t_ff_4_q);
  not not_5 (not_5_out, in_1);
  not not_6 (not_6_out, buffer_1_out);
  not not_7 (not_7_out, buffer_2_out);
  not not_8 (not_8_out, buffer_3_out);
  and and_1 (and_1_out, not_5_out, not_5_out, in_2);
  and and_2 (and_2_out, not_8_out, not_7_out, not_6_out);
  and and_3 (and_3_out, not_8_out, not_7_out, buffer_1_out);
  and and_4 (and_4_out, not_8_out, buffer_2_out, not_6_out);
  and and_5 (and_5_out, not_8_out, buffer_2_out, buffer_1_out);
  and and_6 (and_6_out, buffer_3_out, not_7_out, not_6_out);
  and and_7 (and_7_out, buffer_3_out, not_7_out, buffer_1_out);
  and and_8 (and_8_out, buffer_3_out, buffer_2_out, not_6_out);
  and and_9 (and_9_out, buffer_3_out, buffer_2_out, buffer_1_out);
  and and_10 (and_10_out, and_2_out, and_1_out);
  and and_11 (and_11_out, and_3_out, and_1_out);
  and and_12 (and_12_out, and_4_out, and_1_out);
  and and_13 (and_13_out, and_5_out, and_1_out);
  and and_14 (and_14_out, and_6_out, and_1_out);
  and and_15 (and_15_out, and_7_out, and_1_out);
  and and_16 (and_16_out, and_8_out, and_1_out);
  and and_17 (and_17_out, and_9_out, and_1_out);
  not not_9 (out_4, and_10_out);
  not not_10 (out_5, and_11_out);
  not not_11 (out_6, and_12_out);
  not not_12 (out_7, and_13_out);
  not not_13 (out_8, and_14_out);
  not not_14 (out_9, and_15_out);
  not not_15 (out_10, and_16_out);
  not not_16 (out_11, and_17_out);

  // Notes on the sheet:
  //   Enable is constantly ON 
  //   this pin is not connected on the schematic
endmodule
